// Digital circuit circuito.dig as structural Verilog
module circuito (
  input  clk1,
  input  btn,
  output E0S1,
  output E1S1,
  output ES2,
  output E0S3,
  output E1S3,
  output ES4
);

  wire and_1_out, and_2_out, and_4_out, and_5_out, and_6_out, and_7_out, and_8_out, and_10_out,
       circuito_estados_1_e1, circuito_estados_1_e2, circuito_estados_1_e3, circuito_estados_1_e4,
       circuito_estados_1_ne1, circuito_estados_1_ne2, circuito_estados_1_ne3, circuito_estados_1_ne4,
       not_1_out, rs_ff_as_1_q;

  RS_FF_AS rs_ff_as_1 (.S(btn), .R(not_1_out), .Q(rs_ff_as_1_q));  // open: nQ
  not not_1 (not_1_out, ES4);
  circuito_estados circuito_estados_1 (
    .clk(clk1), .btn(rs_ff_as_1_q), .E1(circuito_estados_1_e1), .nE1(circuito_estados_1_ne1),
    .E2(circuito_estados_1_e2), .nE2(circuito_estados_1_ne2), .E3(circuito_estados_1_e3),
    .nE3(circuito_estados_1_ne3), .E4(circuito_estados_1_e4), .nE4(circuito_estados_1_ne4));
  and and_1 (and_1_out, circuito_estados_1_e2, circuito_estados_1_ne3, circuito_estados_1_e4);
  and and_2 (and_2_out, circuito_estados_1_ne1, circuito_estados_1_ne2, circuito_estados_1_e3, circuito_estados_1_ne4);
  and and_3 (E1S1, circuito_estados_1_ne1, circuito_estados_1_ne2, circuito_estados_1_ne3);
  and and_4 (and_4_out, circuito_estados_1_ne1, circuito_estados_1_ne2, circuito_estados_1_ne3);
  and and_5 (and_5_out, circuito_estados_1_ne3, circuito_estados_1_e4);
  and and_6 (and_6_out, circuito_estados_1_ne1, circuito_estados_1_ne2, circuito_estados_1_e3, circuito_estados_1_ne4);
  and and_7 (and_7_out, circuito_estados_1_e2, circuito_estados_1_ne3, circuito_estados_1_ne4);
  and and_8 (and_8_out, circuito_estados_1_e1, circuito_estados_1_ne3, circuito_estados_1_ne4);
  and and_9 (E1S3, circuito_estados_1_ne1, circuito_estados_1_ne2, circuito_estados_1_e3, circuito_estados_1_e4);
  and and_10 (and_10_out, circuito_estados_1_ne1, circuito_estados_1_ne2, circuito_estados_1_e3);
  or or_1 (ES4, and_10_out, circuito_estados_1_ne3);
  or or_2 (E0S1, and_1_out, and_2_out);
  or or_3 (ES2, and_4_out, and_5_out, and_6_out);
  or or_4 (E0S3, and_7_out, and_8_out);
endmodule
