// Digital circuit circuito_estados.dig as structural Verilog
module circuito_estados (
  input  clk,
  input  btn,
  output E1,
  output nE1,
  output E2,
  output nE2,
  output E3,
  output nE3,
  output E4,
  output nE4
);

  wire and_1_out, and_2_out, and_3_out, and_4_out, and_5_out, and_6_out, and_7_out, and_8_out, and_9_out,
       and_10_out, and_11_out, and_12_out, and_13_out, and_14_out, and_15_out, not_1_out, or_1_out, or_2_out,
       or_3_out;

  D_FF u_E1 (.D(and_1_out), .C(clk), .Q(E1), .nQ(nE1));
  D_FF u_E2 (.D(or_1_out), .C(clk), .Q(E2), .nQ(nE2));
  D_FF u_E3 (.D(or_2_out), .C(clk), .Q(E3), .nQ(nE3));
  D_FF u_E4 (.D(or_3_out), .C(clk), .Q(E4), .nQ(nE4));
  and and_1 (and_1_out, btn, E4, E3, nE2);
  and and_2 (and_2_out, nE3, E1);
  and and_3 (and_3_out, btn, nE3);
  and and_4 (and_4_out, E4, nE3, E2);
  not not_1 (not_1_out, btn);
  or or_1 (or_1_out, and_6_out, and_5_out, and_4_out, and_3_out, and_2_out);
  and and_5 (and_5_out, not_1_out, E4, E3, nE2);
  and and_6 (and_6_out, btn, nE4, E3, nE2);
  and and_7 (and_7_out, nE3, E1);
  and and_8 (and_8_out, btn, nE3, E2);
  or or_2 (or_2_out, and_10_out, and_9_out, and_8_out, and_7_out);
  and and_9 (and_9_out, not_1_out, E4, nE3);
  and and_10 (and_10_out, nE4, E3);
  and and_11 (and_11_out, not_1_out, nE4, nE3, nE2);
  and and_12 (and_12_out, btn, nE4, nE3);
  and and_13 (and_13_out, btn, E4, nE3, nE2);
  or or_3 (or_3_out, and_15_out, and_14_out, and_13_out, and_12_out, and_11_out);
  and and_14 (and_14_out, nE4, E3, E2);
  and and_15 (and_15_out, not_1_out, nE4, E3);
endmodule
