// Digital circuit decoder_sem.dig as structural Verilog
module decoder_sem (
  input  E0,
  input  E1,
  output R,
  output Y,
  output G
);

  xnor xnor_1 (R, E0, E1);
  and and_1 (Y, ~E1, E0);  // And
  and and_2 (G, E1, ~E0);  // And
endmodule
