// Digital circuit main.dig as structural Verilog
module main (
  input  clk
);

  wire button_1_out, circuito_1_e0s1, circuito_1_e0s3, circuito_1_e1s1, circuito_1_e1s3, circuito_1_es2,
       circuito_1_es4, decoder_sem_1_g, decoder_sem_1_r, decoder_sem_1_y, decoder_sem_2_g, decoder_sem_2_r,
       decoder_sem_2_y, not_1_out, not_2_out;

  circuito circuito_1 (
    .clk1(clk), .btn(button_1_out), .E0S1(circuito_1_e0s1), .E1S1(circuito_1_e1s1), .ES2(circuito_1_es2),
    .E0S3(circuito_1_e0s3), .E1S3(circuito_1_e1s3), .ES4(circuito_1_es4));
  LED led_1 (.in(decoder_sem_1_r));
  LED led_2 (.in(decoder_sem_1_y));
  LED led_3 (.in(decoder_sem_1_g));
  decoder_sem decoder_sem_1 (
    .E0(circuito_1_e0s1), .E1(circuito_1_e1s1), .R(decoder_sem_1_r), .Y(decoder_sem_1_y), .G(decoder_sem_1_g));
  LED led_4 (.in(circuito_1_es2));
  LED led_5 (.in(not_1_out));
  not not_1 (not_1_out, circuito_1_es2);
  LED led_6 (.in(decoder_sem_2_r));
  LED led_7 (.in(decoder_sem_2_y));
  LED led_8 (.in(decoder_sem_2_g));
  decoder_sem decoder_sem_2 (
    .E0(circuito_1_e0s3), .E1(circuito_1_e1s3), .R(decoder_sem_2_r), .Y(decoder_sem_2_y), .G(decoder_sem_2_g));
  LED led_9 (.in(circuito_1_es4));
  LED led_10 (.in(not_2_out));
  not not_2 (not_2_out, circuito_1_es4);
  Button button_1 (.out(button_1_out));

  // Notes on the sheet:
  //   S1
  //   S2
  //   S3
  //   S4
endmodule
